// Logisim project Add1bits.circ as structural Verilog: 3 circuits, main circuit main
module main (
  input  a,
  input  b,
  input  c_in,
  output d,
  output c_out
);

  wire and_1_out, and_2_out, and_3_out, xor_1_out;

  xor xor_1 (xor_1_out, a, b);
  and and_1 (and_1_out, a, b);
  and and_2 (and_2_out, a, c_in);
  and and_3 (and_3_out, b, c_in);
  xor xor_2 (d, xor_1_out, c_in);
  or or_1 (c_out, and_1_out, and_2_out, and_3_out);

  // Notes on the sheet:
  //   Attention, votre version de Logisim
  //   ne contient pas de tracker. Si vous
  //   enregistrez votre projet, toutes les
  //   informations du tracker seront
  //   définitivement effacées.
endmodule

module Add1bits (
  input  A,
  input  B,
  input  C_IN,
  output D,
  output C_OUT
);

  wire and_1_out, and_2_out, and_3_out, xor_1_out;

  xor xor_1 (xor_1_out, A, B);
  and and_1 (and_1_out, A, B);
  and and_2 (and_2_out, A, C_IN);
  and and_3 (and_3_out, B, C_IN);
  xor xor_2 (D, xor_1_out, C_IN);
  or or_1 (C_OUT, and_1_out, and_2_out, and_3_out);

  // Notes on the sheet:
  //   Attention, votre version de Logisim
  //   ne contient pas de tracker. Si vous
  //   enregistrez votre projet, toutes les
  //   informations du tracker seront
  //   définitivement effacées.
endmodule

module Add4bits (
  input  C_IN,
  input  [3:0] A,
  input  [3:0] B,
  output [3:0] D,
  output C_OUT
);

  wire Add1bit_0_c_out, Add1bit_1_c_out, Add1bit_2_c_out;

  Add1bits Add1bit_0 (.A(A[0]), .B(B[0]), .C_IN(C_IN), .D(D[0]), .C_OUT(Add1bit_0_c_out));
  Add1bits Add1bit_1 (.A(A[1]), .B(B[1]), .C_IN(Add1bit_0_c_out), .D(D[1]), .C_OUT(Add1bit_1_c_out));
  Add1bits Add1bit_2 (.A(A[2]), .B(B[2]), .C_IN(Add1bit_1_c_out), .D(D[2]), .C_OUT(Add1bit_2_c_out));
  Add1bits Add1bit_3 (.A(A[3]), .B(B[3]), .C_IN(Add1bit_2_c_out), .D(D[3]), .C_OUT(C_OUT));

  // Notes on the sheet:
  //   Attention, votre version de Logisim
  //   ne contient pas de tracker. Si vous
  //   enregistrez votre projet, toutes les
  //   informations du tracker seront
  //   définitivement effacées.
endmodule
