// Logisim project labo_alu_etu.circ as structural Verilog: 11 circuits, main circuit ALU_MAXV
module ALU_MAXV (
  input  [3:0] a_i,
  input  [3:0] b_i,
  output [3:0] c_o,
  output erreur_o
);

  wire [5:0] opcode_i_sw1;

  DipSwitch opcode_i (
    .sw1(opcode_i_sw1[0]), .sw2(opcode_i_sw1[1]), .sw3(opcode_i_sw1[2]), .sw4(opcode_i_sw1[3]),
    .sw5(opcode_i_sw1[4]), .sw6(opcode_i_sw1[5]));  // open: sw7, sw8
  ALU_Top alu_inst (.op_i(opcode_i_sw1), .a_i(a_i), .b_i(b_i), .c_o(c_o), .error_o(erreur_o));

  // Notes on the sheet:
  //   Attention, votre version de Logisim
  //   ne contient pas de tracker. Si vous
  //   enregistrez votre projet, toutes les
  //   informations du tracker seront
  //   définitivement effacées.
endmodule

module ALU_Top (
  input  [5:0] op_i,
  input  [3:0] a_i,
  input  [3:0] b_i,
  output [3:0] c_o,
  output error_o
);

  wire and_1_out, error, math_0_c_o, math_0_n_o, math_0_z_o, ov;
  wire [1:0] multiplex;
  wire [3:0] comp_op, comp_r, custom_r, logic_op, logic_r, math_op, math_r;

  Math math_0 (
    .op_i(math_op), .a_i(a_i), .b_i(b_i), .r_o(math_r), .c_o(math_0_c_o), .z_o(math_0_z_o), .n_o(math_0_n_o),
    .ov_o(ov));
  Logic logic_o (.op_i(logic_op), .a_i(a_i), .b_i(b_i), .logic_o(logic_r));
  Multiplexer #(.select(2), .width(4), .enable("false")) multiplexer_1 (
    .in0(math_r), .in1(comp_r), .in2(logic_r), .in3(custom_r), .out(c_o), .sel(multiplex));
  Comp comp_0 (.op_i(comp_op), .c_i(math_0_c_o), .z_i(math_0_z_o), .n_i(math_0_n_o), .cmp_o(comp_r));
  and and_1 (and_1_out, ov, ~multiplex[0], ~multiplex[1]);  // AND_Gate
  Opselect opselect_0 (
    .op_i(op_i), .math_o(math_op), .comp_o(comp_op), .logic_o(logic_op), .multiplex_o(multiplex),
    .erreur_o(error));
  Custom custom_0 (.a_i(a_i), .custom_o(custom_r));
  or or_1 (error_o, and_1_out, error);

  // Other names for the same wires on the sheet: a[3:0] = a_i; b[3:0] = b_i; op[5:0] = op_i

  // Notes on the sheet:
  //   Attention, votre version de Logisim
  //   ne contient pas de tracker. Si vous
  //   enregistrez votre projet, toutes les
  //   informations du tracker seront
  //   définitivement effacées.
endmodule

module Math (
  input  [3:0] op_i,
  input  [3:0] a_i,
  input  [3:0] b_i,
  output [3:0] r_o,
  output c_o,
  output z_o,
  output n_o,
  output ov_o
);

  wire cp;

  AddSub4Bit AddSub4bit_0 (.sel_i(op_i[3]), .a_i(a_i), .b_i(b_i), .r_o(r_o), .cp_o(cp), .c_o(c_o));
  nor nor_1 (z_o, r_o[0], r_o[1], r_o[2], r_o[3]);
  xor xor_1 (ov_o, c_o, cp);
  xor xor_2 (n_o, r_o[3], ov_o);

  // Other names for the same wires on the sheet: c = c_o; op[3:0] = op_i; r[3:0] = r_o

  // Notes on the sheet:
  //   Attention, votre version de Logisim
  //   ne contient pas de tracker. Si vous
  //   enregistrez votre projet, toutes les
  //   informations du tracker seront
  //   définitivement effacées.
  //   carry n xor carry n-1
endmodule

module Comp (
  input  [3:0] op_i,
  input  c_i,
  input  z_i,
  input  n_i,
  output [3:0] cmp_o
);

  wire and_1_out, and_2_out, and_3_out, and_4_out, and_5_out, and_6_out;

  and and_1 (and_1_out, ~n_i, ~op_i[2], op_i[0], ~op_i[1]);  // AND_Gate
  and and_2 (and_2_out, n_i, ~op_i[2], ~op_i[0], op_i[1]);  // AND_Gate
  and and_3 (and_3_out, ~z_i, op_i[0], op_i[1]);  // AND_Gate
  and and_4 (and_4_out, z_i, ~op_i[0], ~op_i[1]);  // AND_Gate
  and and_5 (and_5_out, c_i, op_i[2], op_i[0], ~op_i[1]);  // AND_Gate
  and and_6 (and_6_out, ~c_i, op_i[2], ~op_i[0], op_i[1]);  // AND_Gate
  or or_1 (cmp_o[0], and_1_out, and_2_out, and_3_out, and_4_out, and_5_out, and_6_out);

  assign cmp_o[3:1] = 3'b000;

  // Other names for the same wires on the sheet: c = c_i; n = n_i; op[3:0] = op_i; s = op_i[2]; z = z_i

  // Notes on the sheet:
  //   Attention, votre version de Logisim
  //   ne contient pas de tracker. Si vous
  //   enregistrez votre projet, toutes les
  //   informations du tracker seront
  //   définitivement effacées.
  //   A >= B (signed)
  //   A < B (signed)
  //   A !=B
  //   A = B
  //   A >= B (unsigned)
  //   A < B (unsigned)
endmodule

module Logic (
  input  [3:0] op_i,
  input  [3:0] a_i,
  input  [3:0] b_i,
  output [3:0] logic_o
);

  wire [3:0] and_1_out, nand_1_out, or_1_out, xor_1_out;

  assign and_1_out = b_i & a_i;  // AND_Gate and_1, 4 bits wide
  assign or_1_out = b_i | a_i;  // OR_Gate or_1, 4 bits wide
  assign nand_1_out = ~(b_i & a_i);  // NAND_Gate nand_1, 4 bits wide
  assign xor_1_out = b_i ^ a_i;  // XOR_Gate xor_1, 4 bits wide
  Multiplexer #(.select(2), .width(4), .enable("false")) multiplexer_1 (
    .in0(and_1_out), .in1(or_1_out), .in2(nand_1_out), .in3(xor_1_out), .out(logic_o), .sel(op_i[1:0]));

  // Other names for the same wires on the sheet: a[3:0] = a_i; b[3:0] = b_i; op[1:0] = op_i[1:0]

  // Notes on the sheet:
  //   Attention, votre version de Logisim
  //   ne contient pas de tracker. Si vous
  //   enregistrez votre projet, toutes les
  //   informations du tracker seront
  //   définitivement effacées.
endmodule

module Custom (
  input  [3:0] a_i,
  output [3:0] custom_o
);

  wire [1:0] Add1bit_0_r_o, Add1bit_1_r_o;

  Add1Bit Add1bit_0 (.a_i(a_i[0]), .b_i(a_i[1]), .c_i(1'b0), .r_o(Add1bit_0_r_o[0]), .c_o(Add1bit_0_r_o[1]));
  Add1Bit Add1bit_1 (.a_i(a_i[2]), .b_i(a_i[3]), .c_i(1'b0), .r_o(Add1bit_1_r_o[0]), .c_o(Add1bit_1_r_o[1]));
  Add4bit Add4bit_0 (
    .c_i(1'b0), .a_i({2'b00, Add1bit_0_r_o}), .b_i({2'b00, Add1bit_1_r_o}), .r_o(custom_o));  // open: cp_o, c_o

  // Notes on the sheet:
  //   Attention, votre version de Logisim
  //   ne contient pas de tracker. Si vous
  //   enregistrez votre projet, toutes les
  //   informations du tracker seront
  //   définitivement effacées.
endmodule

module Opselect (
  input  [5:0] op_i,
  output [3:0] math_o,
  output [3:0] comp_o,
  output [3:0] logic_o,
  output [1:0] multiplex_o,
  output erreur_o
);

  wire [3:0] and_1_out;
  wire [3:3] nor_1_out, nor_2_out, nor_3_out;

  nor nor_1 (nor_1_out[3], op_i[4], op_i[5]);
  nor nor_2 (nor_2_out[3], ~op_i[4], op_i[5]);  // NOR_Gate
  nor nor_3 (nor_3_out[3], op_i[4], ~op_i[5]);  // NOR_Gate
  assign and_1_out = op_i[3:0] & {4{nor_1_out[3]}};  // AND_Gate and_1, 4 bits wide
  assign comp_o = op_i[3:0] & {4{nor_2_out[3]}};  // AND_Gate and_2, 4 bits wide
  assign logic_o = op_i[3:0] & {4{nor_3_out[3]}};  // AND_Gate and_3, 4 bits wide
  OpError operror_1 (.op_i(op_i), .error_r(erreur_o));
  assign math_o = and_1_out | comp_o;  // OR_Gate or_1, 4 bits wide

  assign multiplex_o = op_i[5:4];

  // Notes on the sheet:
  //   Attention, votre version de Logisim
  //   ne contient pas de tracker. Si vous
  //   enregistrez votre projet, toutes les
  //   informations du tracker seront
  //   définitivement effacées.
  //   Math
  //   Comparator
  //   Logic
endmodule

module OpError (
  input  [5:0] op_i,
  output error_r
);

  wire and_1_out, and_2_out, and_3_out;

  and and_1 (and_1_out, op_i[0], op_i[1], op_i[2], 1'b1, op_i[4], ~op_i[5]);  // AND_Gate
  and and_2 (and_2_out, ~op_i[0], ~op_i[1], ~op_i[2], op_i[3], op_i[4], ~op_i[5]);  // AND_Gate
  and and_3 (and_3_out, op_i[2], ~op_i[3], op_i[4], ~op_i[5]);  // AND_Gate
  or or_1 (error_r, and_1_out, and_2_out, and_3_out);

  // Notes on the sheet:
  //   Attention, votre version de Logisim
  //   ne contient pas de tracker. Si vous
  //   enregistrez votre projet, toutes les
  //   informations du tracker seront
  //   définitivement effacées.
endmodule

module AddSub4Bit (
  input  sel_i,
  input  [3:0] a_i,
  input  [3:0] b_i,
  output [3:0] r_o,
  output cp_o,
  output c_o
);

  wire [3:0] xor_1_out;

  assign xor_1_out = b_i ^ {4{sel_i}};  // XOR_Gate xor_1, 4 bits wide
  Add4bit Add4bit_0 (.c_i(sel_i), .a_i(a_i), .b_i(xor_1_out), .r_o(r_o), .cp_o(cp_o), .c_o(c_o));

  // Notes on the sheet:
  //   Attention, votre version de Logisim
  //   ne contient pas de tracker. Si vous
  //   enregistrez votre projet, toutes les
  //   informations du tracker seront
  //   définitivement effacées.
endmodule

module Add4bit (
  input  c_i,
  input  [3:0] a_i,
  input  [3:0] b_i,
  output [3:0] r_o,
  output cp_o,
  output c_o
);

  wire Add1Bit_0_c_o, Add1Bit_1_c_o;

  Add1Bit Add1Bit_0 (.a_i(a_i[0]), .b_i(b_i[0]), .c_i(c_i), .r_o(r_o[0]), .c_o(Add1Bit_0_c_o));
  Add1Bit Add1Bit_1 (.a_i(a_i[1]), .b_i(b_i[1]), .c_i(Add1Bit_0_c_o), .r_o(r_o[1]), .c_o(Add1Bit_1_c_o));
  Add1Bit Add1Bit_2 (.a_i(a_i[2]), .b_i(b_i[2]), .c_i(Add1Bit_1_c_o), .r_o(r_o[2]), .c_o(cp_o));
  Add1Bit Add1Bit_3 (.a_i(a_i[3]), .b_i(b_i[3]), .c_i(cp_o), .r_o(r_o[3]), .c_o(c_o));

  // Notes on the sheet:
  //   Attention, votre version de Logisim
  //   ne contient pas de tracker. Si vous
  //   enregistrez votre projet, toutes les
  //   informations du tracker seront
  //   définitivement effacées.
endmodule

module Add1Bit (
  input  a_i,
  input  b_i,
  input  c_i,
  output r_o,
  output c_o
);

  wire and_1_out, and_2_out, and_3_out, xor_1_out;

  xor xor_1 (xor_1_out, a_i, b_i);
  and and_1 (and_1_out, a_i, b_i);
  and and_2 (and_2_out, a_i, c_i);
  and and_3 (and_3_out, b_i, c_i);
  xor xor_2 (r_o, xor_1_out, c_i);
  or or_1 (c_o, and_1_out, and_2_out, and_3_out);

  // Notes on the sheet:
  //   Attention, votre version de Logisim
  //   ne contient pas de tracker. Si vous
  //   enregistrez votre projet, toutes les
  //   informations du tracker seront
  //   définitivement effacées.
endmodule
