// Logisim project labo_chenillard_etu.circ as structural Verilog: 5 circuits, main circuit MAXV_CHENILLARD
module MAXV_CHENILLARD (
  input  clk_i,
  input  nReset_i,
  input  load_i,
  input  [7:0] switch_i,
  output [7:0] led_o
);

  wire entree_i_sw7, entree_i_sw8, not_1_out;
  wire [1:0] entree_i_sw2;

  DipSwitch entree_i (
    .sw1(entree_i_sw2[1]), .sw2(entree_i_sw2[0]), .sw7(entree_i_sw7), .sw8(entree_i_sw8));  // open: sw3, sw4, sw5, sw6
  Clock sysclk ();  // open: out
  Clock #(.highDuration(2), .lowDuration(2)) clk_test ();  // open: out
  not not_1 (not_1_out, nReset_i);
  chenillard_TOP chenillard (
    .clk_i(clk_i), .reset_i(not_1_out), .load_i(load_i), .speed_i(entree_i_sw2), .enable_i(entree_i_sw7),
    .right_nleft_i(entree_i_sw8), .val_i(switch_i), .led_o(led_o));

  // Notes on the sheet:
  //   Attention, votre version de Logisim
  //   ne contient pas de tracker. Si vous
  //   enregistrez votre projet, toutes les
  //   informations du tracker seront
  //   définitivement effacées.
  //   Pour le chronogramme
endmodule

module chenillard_TOP (
  input  clk_i,
  input  reset_i,
  input  load_i,
  input  [1:0] speed_i,
  input  enable_i,
  input  right_nleft_i,
  input  [7:0] val_i,
  output [7:0] led_o
);

  wire done_o;
  wire [1:0] multiplexer_1_out;
  wire [27:0] multiplexer_2_out;

  Multiplexer #(.select(2), .width(2), .enable("false")) multiplexer_1 (
    .in0(2'b00), .in1({1'b1, right_nleft_i}), .in2({1'b0, load_i}), .in3(2'b00), .out(multiplexer_1_out),
    .sel({load_i, done_o}));
  Multiplexer #(.select(2), .width(28), .enable("false")) multiplexer_2 (
    .in0(28'hf8d8f20), .in1(28'hf1b1e40), .in2(28'he363c80), .in3(28'hc6c7900), .out(multiplexer_2_out),
    .sel(speed_i));
  timer_28b timer_28b_1 (
    .load_i(1'b0), .en_i(enable_i), .value_i(multiplexer_2_out), .clk_i(clk_i), .reset_i(reset_i),
    .done_o(done_o));
  shift_reg_8b reg_8b_1 (
    .clk_i(clk_i), .mode_i(multiplexer_1_out), .reset_i(reset_i), .value_load_i(val_i), .ser_r_i(led_o[0]),
    .ser_l_i(led_o[7]), .val_o(led_o));

  // Other names for the same wires on the sheet: lsb = led_o[0]; msb = led_o[7]

  // Notes on the sheet:
  //   Attention, votre version de Logisim
  //   ne contient pas de tracker. Si vous
  //   enregistrez votre projet, toutes les
  //   informations du tracker seront
  //   définitivement effacées.
  //   4 Hz
  //   2 Hz
  //   1 Hz
  //   0.5 Hz
endmodule

module shift_reg_4b (
  input  [3:0] value_load_i,
  input  ser_r_i,
  input  ser_l_i,
  input  [1:0] mode_i,
  input  clk_i,
  input  reset_i,
  output [3:0] val_o
);

  wire multiplexer_1_out, multiplexer_2_out, multiplexer_3_out, multiplexer_4_out;

  Multiplexer #(.select(2), .enable("false")) multiplexer_1 (
    .in0(val_o[3]), .in1(value_load_i[3]), .in2(val_o[2]), .in3(ser_r_i), .out(multiplexer_1_out),
    .sel(mode_i));
  D_Flip_Flop D_4 (.D(multiplexer_1_out), .clk(clk_i), .Q(val_o[3]), .reset(reset_i));  // open: Qn, preset
  Multiplexer #(.select(2), .enable("false")) multiplexer_2 (
    .in0(val_o[2]), .in1(value_load_i[2]), .in2(val_o[1]), .in3(val_o[3]), .out(multiplexer_2_out),
    .sel(mode_i));
  D_Flip_Flop D_3 (.D(multiplexer_2_out), .clk(clk_i), .Q(val_o[2]), .reset(reset_i));  // open: Qn, preset
  Multiplexer #(.select(2), .enable("false")) multiplexer_3 (
    .in0(val_o[1]), .in1(value_load_i[1]), .in2(val_o[0]), .in3(val_o[2]), .out(multiplexer_3_out),
    .sel(mode_i));
  D_Flip_Flop D_2 (.D(multiplexer_3_out), .clk(clk_i), .Q(val_o[1]), .reset(reset_i));  // open: Qn, preset
  Multiplexer #(.select(2), .enable("false")) multiplexer_4 (
    .in0(val_o[0]), .in1(value_load_i[0]), .in2(ser_l_i), .in3(val_o[1]), .out(multiplexer_4_out),
    .sel(mode_i));
  D_Flip_Flop D_1 (.D(multiplexer_4_out), .clk(clk_i), .Q(val_o[0]), .reset(reset_i));  // open: Qn, preset

  // Other names for the same wires on the sheet: mode[1:0] = mode_i; l_1 = value_load_i[0]; l_2 = value_load_i[1];
  //   l_3 = value_load_i[2]; l_4 = value_load_i[3]

  // Notes on the sheet:
  //   Attention, votre version de Logisim
  //   ne contient pas de tracker. Si vous
  //   enregistrez votre projet, toutes les
  //   informations du tracker seront
  //   définitivement effacées.
endmodule

module shift_reg_8b (
  input  clk_i,
  input  [1:0] mode_i,
  input  reset_i,
  input  [7:0] value_load_i,
  input  ser_r_i,
  input  ser_l_i,
  output [7:0] val_o
);

  shift_reg_4b reg_4b_1 (
    .value_load_i(value_load_i[7:4]), .ser_r_i(ser_r_i), .ser_l_i(val_o[3]), .mode_i(mode_i), .clk_i(clk_i),
    .reset_i(reset_i), .val_o(val_o[7:4]));
  shift_reg_4b reg_4b_2 (
    .value_load_i(value_load_i[3:0]), .ser_r_i(val_o[4]), .ser_l_i(ser_l_i), .mode_i(mode_i), .clk_i(clk_i),
    .reset_i(reset_i), .val_o(val_o[3:0]));

  // Other names for the same wires on the sheet: mode[1:0] = mode_i; reset = reset_i; reg_2_msb = val_o[3];
  //   reg_1_lsb = val_o[4]; load_4b_2[3:0] = value_load_i[3:0]; load_4b_1[3:0] = value_load_i[7:4]

  // Notes on the sheet:
  //   Attention, votre version de Logisim
  //   ne contient pas de tracker. Si vous
  //   enregistrez votre projet, toutes les
  //   informations du tracker seront
  //   définitivement effacées.
endmodule

module timer_28b (
  input  load_i,
  input  en_i,
  input  [27:0] value_i,
  input  clk_i,
  input  reset_i,
  output done_o
);

  wire comparator_1_eq, or_1_out;
  wire [27:0] adder_1_out, multiplexer_1_out, o_r;

  Comparator #(.width(28)) comparator_1 (.a(o_r), .b({28{1'b0}}), .eq(comparator_1_eq));  // open: gt, lt
  Adder #(.width(28)) adder_1 (.a({{27{1'b0}}, en_i}), .b(o_r), .out(adder_1_out));  // open: cin, cout
  or or_1 (or_1_out, done_o, comparator_1_eq);
  Multiplexer #(.width(28), .enable("false")) multiplexer_1 (
    .in0(adder_1_out), .in1(value_i), .out(multiplexer_1_out), .sel(or_1_out));
  Register #(.width(28)) register_1 (.D(multiplexer_1_out), .en(en_i), .clk(clk_i), .Q(o_r), .clr(reset_i));
  and and_1 (done_o, o_r[0], o_r[1], o_r[2], o_r[3], o_r[4], o_r[5], o_r[6], o_r[7], o_r[8], o_r[9], o_r[10], o_r[11], o_r[12], o_r[13], o_r[14], o_r[15], o_r[16], o_r[17], o_r[18], o_r[19], o_r[20], o_r[21], o_r[22], o_r[23], o_r[24], o_r[25], o_r[26], o_r[27]);

  // Notes on the sheet:
  //   Attention, votre version de Logisim
  //   ne contient pas de tracker. Si vous
  //   enregistrez votre projet, toutes les
  //   informations du tracker seront
  //   définitivement effacées.
endmodule
