// Logisim project laboratoire_Tapis_de_triage.circ as structural Verilog: 7 circuits, main circuit sim_console_tapis_triage
module sim_console_tapis_triage (
);

  wire sysclk_out, tapis_triage_console_p1, tapis_triage_console_p2, tapis_triage_console_p3,
       tapis_triage_console_p4, tapis_triage_console_p5, tapis_triage_console_p8, tapis_triage_console_p9,
       tapis_triage_console_p10;
  wire [1:0] tapis_triage_console_p6;
  wire [15:0] tapis_triage_console_p11;

  Clock sysclk (.out(sysclk_out));
  // TclConsoleReds #(.filePath("..\\Documents\\labos-SYL-test\\SYL\\aro\\Tapis_Triage_Logisim\\tapis_triage\\console\\Console_Tapis_triage.tcl")) tapis_triage_console: pin names not known; wires that end beside it: tapis_triage_console_p1, tapis_triage_console_p2, tapis_triage_console_p3, tapis_triage_console_p4, tapis_triage_console_p5, {{14{1'b0}}, tapis_triage_console_p6}, sysclk_out, tapis_triage_console_p8, tapis_triage_console_p9, tapis_triage_console_p10, tapis_triage_console_p11
  tapis_triage_top Tapis_Tri_Top (
    .capt_fin_tapis2_i(tapis_triage_console_p11[6]), .capt_lg_i(tapis_triage_console_p11[3]),
    .capt_mot_i(tapis_triage_console_p11[0]), .capt_piece1_i(tapis_triage_console_p11[2]),
    .capt_v1_i(tapis_triage_console_p11[4]), .capt_v2_i(tapis_triage_console_p11[5]),
    .defect_i(tapis_triage_console_p11[1]), .v1_in_i(tapis_triage_console_p11[7]),
    .v2_in_i(tapis_triage_console_p8), .v2_out_i(tapis_triage_console_p9),
    .mot_tapis1_o(tapis_triage_console_p4), .mot_tapis2_o(tapis_triage_console_p5),
    .rentrer_v2_o(tapis_triage_console_p3), .sortir_v1_o(tapis_triage_console_p1),
    .sortir_v2_o(tapis_triage_console_p2), .nRst_i(tapis_triage_console_p10), .clk_i(sysclk_out),
    .code_lg_o(tapis_triage_console_p6));

  // Notes on the sheet:
  //   Attention, votre version de Logisim
  //   ne contient pas de tracker. Si vous
  //   enregistrez votre projet, toutes les
  //   informations du tracker seront
  //   définitivement effacées.
endmodule

module tapis_triage_top (
  input  capt_fin_tapis2_i,
  input  capt_lg_i,
  input  capt_mot_i,
  input  capt_piece1_i,
  input  capt_v1_i,
  input  capt_v2_i,
  input  defect_i,
  input  v1_in_i,
  input  v2_in_i,
  input  v2_out_i,
  input  nRst_i,
  input  clk_i,
  output mot_tapis1_o,
  output mot_tapis2_o,
  output sortir_v1_o,
  output sortir_v2_o,
  output rentrer_v2_o,
  output [1:0] code_lg_o
);

  wire I0_valide_lg_o, I2_new_box_o, L_Tapis_de_tri2_give_o, not_1_out;
  wire [7:0] I0_valeur_o;

  not not_1 (not_1_out, nRst_i);
  Tapis_Intro_logisim I2 (
    .capt_piece1_i(capt_piece1_i), .give_i(L_Tapis_de_tri2_give_o), .clk_i(clk_i), .reset_i(not_1_out),
    .mot_tapis1_o(mot_tapis1_o), .new_box_o(I2_new_box_o));
  Mesure_Lg_logisim I0 (
    .capt_lg_i(capt_lg_i), .capt_mot_i(capt_mot_i), .clk_i(clk_i), .reset_i(not_1_out),
    .valide_lg_o(I0_valide_lg_o), .valeur_o(I0_valeur_o));
  code_lg_simulation I1 (.val_compteur_i(I0_valeur_o), .code_o(code_lg_o));
  tapis_de_tri_2 L_Tapis_de_tri2 (
    .reset(not_1_out), .v2_out_i(v2_out_i), .capt_v1_i(capt_v1_i), .new_box_i(I2_new_box_o),
    .capt_fin_tapis2_i(capt_fin_tapis2_i), .v1_in_i(v1_in_i), .valide_lg_i(I0_valide_lg_o),
    .capt_v2_i(capt_v2_i), .code_lg_i(code_lg_o), .v2_in_i(v2_in_i), .give_o(L_Tapis_de_tri2_give_o),
    .mot_tapis2_o(mot_tapis2_o), .sortir_v1_o(sortir_v1_o), .sortir_v2_o(sortir_v2_o),
    .rentrer_v2_o(rentrer_v2_o), .defect_i(defect_i), .clock(clk_i));

  // Notes on the sheet:
  //   Attention, votre version de Logisim
  //   ne contient pas de tracker. Si vous
  //   enregistrez votre projet, toutes les
  //   informations du tracker seront
  //   définitivement effacées.
  //   Remarque : Veuillez éviter toute modifications dans le circuit 
  //   Gestion tapis1
  //   Mesure longueur
endmodule

module tapis_de_tri_2 (
  input  new_box_i,
  input  defect_i,
  input  valide_lg_i,
  input  [1:0] code_lg_i,
  input  capt_v1_i,
  input  capt_v2_i,
  input  capt_fin_tapis2_i,
  input  v1_in_i,
  input  v2_in_i,
  input  v2_out_i,
  input  clock,
  input  reset,
  output give_o,
  output mot_tapis2_o,
  output sortir_v1_o,
  output sortir_v2_o,
  output rentrer_v2_o
);

  wire and_1_out, and_2_out, and_3_out, and_4_out, and_5_out, and_6_out, and_7_out, and_8_out, and_9_out,
       and_10_out, and_11_out, and_12_out, and_13_out, and_14_out, and_15_out, and_16_out, and_17_out,
       and_18_out, and_19_out, and_20_out, and_21_out, and_22_out, and_23_out, and_24_out, and_25_out,
       and_26_out, idle, move_piston, move_trash, move_validation, or_1_out, or_2_out, or_3_out, or_4_out,
       or_5_out, or_6_out, or_7_out, or_8_out, or_9_out, or_10_out, or_11_out, or_13_out, trash, validation,
       xnor_1_out, xor_1_out;

  xnor xnor_1 (xnor_1_out, code_lg_i[0], code_lg_i[1]);
  and and_1 (and_1_out, valide_lg_i, xnor_1_out);
  or or_1 (or_1_out, move_validation, validation);
  or or_2 (or_2_out, defect_i, and_1_out);
  and and_2 (and_2_out, rentrer_v2_o, v2_in_i);
  and and_3 (and_3_out, trash, ~capt_fin_tapis2_i);  // AND_Gate
  and and_4 (and_4_out, sortir_v1_o, v1_in_i);
  and and_5 (and_5_out, idle, ~new_box_i);  // AND_Gate
  or or_3 (or_3_out, idle, give_o);
  and and_6 (and_6_out, give_o, ~new_box_i);  // AND_Gate
  and and_7 (and_7_out, move_validation, ~defect_i, valide_lg_i);  // AND_Gate
  and and_8 (and_8_out, validation, or_2_out);
  and and_9 (and_9_out, move_trash, ~capt_fin_tapis2_i);  // AND_Gate
  and and_10 (and_10_out, move_validation, defect_i);
  or or_4 (or_4_out, move_trash, trash);
  and and_11 (and_11_out, or_3_out, new_box_i);
  or or_5 (or_5_out, and_6_out, and_7_out);
  and and_12 (and_12_out, or_1_out, ~defect_i, ~valide_lg_i);  // AND_Gate
  or or_6 (or_6_out, and_8_out, and_9_out, and_10_out);
  or or_7 (or_7_out, and_2_out, and_3_out, and_4_out, and_5_out);
  D_Flip_Flop D_ff_1 (.D(and_11_out), .clk(clock), .Q(give_o), .reset(reset));  // open: Qn, preset
  and and_13 (and_13_out, and_12_out, ~move_trash);  // AND_Gate
  and and_14 (and_14_out, or_4_out, capt_fin_tapis2_i);
  D_Flip_Flop D_ff_0 (.D(or_7_out), .clk(clock), .Q(idle), .preset(reset));  // open: Qn, reset
  D_Flip_Flop D_ff_2 (.D(or_5_out), .clk(clock), .Q(move_validation), .reset(reset));  // open: Qn, preset
  D_Flip_Flop D_ff_3 (.D(and_13_out), .clk(clock), .Q(validation), .reset(reset));  // open: Qn, preset
  D_Flip_Flop D_ff_4 (.D(or_6_out), .clk(clock), .Q(move_trash), .reset(reset));  // open: Qn, preset
  D_Flip_Flop D_ff_9 (.D(and_14_out), .clk(clock), .Q(trash), .reset(reset));  // open: Qn, preset
  xor xor_1 (xor_1_out, code_lg_i[0], code_lg_i[1]);
  and and_15 (and_15_out, code_lg_i[0], ~code_lg_i[1]);  // AND_Gate
  and and_16 (and_16_out, ~code_lg_i[0], code_lg_i[1]);  // AND_Gate
  and and_17 (and_17_out, validation, xor_1_out, valide_lg_i);
  and and_18 (and_18_out, move_piston, or_8_out);
  and and_19 (and_19_out, and_15_out, ~capt_v1_i);  // AND_Gate
  and and_20 (and_20_out, and_16_out, ~capt_v2_i);  // AND_Gate
  and and_21 (and_21_out, move_piston, and_15_out, capt_v1_i);
  and and_22 (and_22_out, sortir_v1_o, ~v1_in_i);  // AND_Gate
  and and_23 (and_23_out, move_piston, and_16_out, capt_v2_i);
  and and_24 (and_24_out, sortir_v2_o, ~v2_out_i);  // AND_Gate
  and and_25 (and_25_out, sortir_v2_o, v2_out_i);
  and and_26 (and_26_out, rentrer_v2_o, ~v2_in_i);  // AND_Gate
  or or_8 (or_8_out, and_19_out, and_20_out);
  or or_9 (or_9_out, and_21_out, and_22_out);
  or or_10 (or_10_out, and_23_out, and_24_out);
  or or_11 (or_11_out, and_25_out, and_26_out);
  or or_12 (mot_tapis2_o, give_o, move_validation, validation, move_piston, move_trash, trash);
  D_Flip_Flop D_ff_5 (.D(or_13_out), .clk(clock), .Q(move_piston), .reset(reset));  // open: Qn, preset
  or or_13 (or_13_out, and_17_out, and_18_out);
  D_Flip_Flop D_ff_6 (.D(or_9_out), .clk(clock), .Q(sortir_v1_o), .reset(reset));  // open: Qn, preset
  D_Flip_Flop D_ff_7 (.D(or_10_out), .clk(clock), .Q(sortir_v2_o), .reset(reset));  // open: Qn, preset
  D_Flip_Flop D_ff_8 (.D(or_11_out), .clk(clock), .Q(rentrer_v2_o), .reset(reset));  // open: Qn, preset

  // Other names for the same wires on the sheet: clk = clock; new_box = give_o; v1 = sortir_v1_o;
  //   v2_pull = rentrer_v2_o; v2_push = sortir_v2_o

  // Notes on the sheet:
  //   Attention, votre version de Logisim
  //   ne contient pas de tracker. Si vous
  //   enregistrez votre projet, toutes les
  //   informations du tracker seront
  //   définitivement effacées.
  //   A =( ( / (code_lg_i_0 ^ code_lg_i_1) * valide_lg_i) + defect_i ) * validation
  //   move_trash = A + (move_trash * /capt_fin_tapis2_i) + (move_validation * defect_i)
  //   A
  //   idle = v2_pull * v2_in_1 + trash * /capt_fin_tapis2_i + v1 * v1_in_i + idle * new_box_i
  //   new_box = (idle + new_box) * new_box_i 
  //   move_validation = (new_box * /new_box_i) + (move_validation * /defect_i * valid_lg_i) 
  //   validation = ( (move_validation + validation) * /defect_i * /valid_lg_i ) * /move_trash
  //   trash = (move_trash + trash) * capt_fin_tapis2_i
  //   A
  //   B
  //   C
  //   v1 = (move_piston * (code_lg_i_0 * / code_lg_i_1) * capt_v1_i) + (v1 * /v1_in_i)
  //   v2_push = (move_piston * (/code_lg_i_0 * code_lg_i_1) + (v2_push * / v2_out_i))
  //   B = /capt_v1_i * (code_lg_i_0 * /code_lg_i_1)
  //   C = /capt_v2_i * (/code_lg_i_0 * code_lg_i_1)
  //   move_piston = A + (move_piston * (B + C) )
  //   v2_pull = (v2_push * v2_out_i) + (v2_pull * /v2_in_i)
  //   A = validation * (code_lg_i_0 ^ code_lg_i_1) * valide_lg_i
endmodule

module Mesure_Lg_logisim (
  input  capt_lg_i,
  input  capt_mot_i,
  input  clk_i,
  input  reset_i,
  output valide_lg_o,
  output [7:0] valeur_o
);

  wire and_1_out, and_2_out, and_3_out, d_ff_1_q, d_ff_2_q, d_ff_3_q, multiplexer_3_out, multiplexer_4_out;
  wire [7:0] adder_1_out, multiplexer_1_out, multiplexer_2_out;

  D_Flip_Flop d_ff_1 (.D(capt_lg_i), .clk(clk_i), .Q(d_ff_1_q), .preset(1'b0), .reset(reset_i));  // open: Qn
  Adder adder_1 (.a(valeur_o), .b(8'h1), .out(adder_1_out), .cin(1'b0));  // open: cout
  D_Flip_Flop d_ff_2 (.D(d_ff_1_q), .clk(clk_i), .Q(d_ff_2_q), .preset(1'b0), .reset(reset_i));  // open: Qn
  D_Flip_Flop d_ff_3 (.D(d_ff_1_q), .clk(clk_i), .Q(d_ff_3_q), .preset(1'b0), .reset(reset_i));  // open: Qn
  and and_1 (and_1_out, d_ff_1_q, ~and_3_out, ~and_2_out);  // AND_Gate
  Multiplexer #(.width(8), .enable("false")) multiplexer_1 (
    .in0(valeur_o), .in1(adder_1_out), .out(multiplexer_1_out), .sel(and_1_out));
  and and_2 (and_2_out, ~d_ff_1_q, d_ff_2_q);  // AND_Gate
  and and_3 (and_3_out, d_ff_1_q, ~d_ff_3_q);  // AND_Gate
  Register Longueur (.D(multiplexer_2_out), .en(1'b1), .clk(clk_i), .Q(valeur_o), .clr(reset_i));
  Multiplexer #(.width(8), .enable("false")) multiplexer_2 (
    .in0(multiplexer_1_out), .in1({8{1'b0}}), .out(multiplexer_2_out), .sel(and_3_out));
  Multiplexer #(.enable("false")) multiplexer_3 (
    .in0(valide_lg_o), .in1(1'b1), .out(multiplexer_3_out), .sel(and_2_out));
  Multiplexer #(.enable("false")) multiplexer_4 (
    .in0(multiplexer_3_out), .in1(1'b0), .out(multiplexer_4_out), .sel(and_3_out));
  D_Flip_Flop d_ff_4 (.D(multiplexer_4_out), .clk(clk_i), .Q(valide_lg_o), .preset(1'b0), .reset(reset_i));  // open: Qn

  // Notes on the sheet:
  //   Attention, votre version de Logisim
  //   ne contient pas de tracker. Si vous
  //   enregistrez votre projet, toutes les
  //   informations du tracker seront
  //   définitivement effacées.
  //   Not used at the moment
  //   Falling edge
  //   Rising edge
endmodule

module Tapis_Intro_logisim (
  input  capt_piece1_i,
  input  give_i,
  input  clk_i,
  input  reset_i,
  output mot_tapis1_o,
  output new_box_o
);

  wire [1:0] multiplexer_1_out, multiplexer_2_out, multiplexer_3_out, multiplexer_4_out, multiplexer_5_out,
       multiplexer_6_out, register_1_q;

  Multiplexer #(.width(2), .enable("false")) multiplexer_1 (
    .in0(2'b00), .in1(2'b01), .out(multiplexer_1_out), .sel(capt_piece1_i));
  Multiplexer #(.width(2), .enable("false")) multiplexer_2 (
    .in0(2'b01), .in1(2'b11), .out(multiplexer_2_out), .sel(give_i));
  Multiplexer #(.width(2), .enable("false")) multiplexer_3 (
    .in0(2'b00), .in1(multiplexer_4_out), .out(multiplexer_3_out), .sel(capt_piece1_i));
  Multiplexer #(.width(2), .enable("false")) multiplexer_4 (
    .in0(2'b01), .in1(2'b10), .out(multiplexer_4_out), .sel(give_i));
  Multiplexer #(.width(2), .enable("false")) multiplexer_5 (
    .in0(2'b01), .in1(2'b10), .out(multiplexer_5_out), .sel(give_i));
  Multiplexer #(.select(2), .width(2), .enable("false")) multiplexer_6 (
    .in0(multiplexer_1_out), .in1(multiplexer_2_out), .in2(multiplexer_3_out), .in3(multiplexer_5_out),
    .out(multiplexer_6_out), .sel(register_1_q));
  // Probe on multiplexer_6_out
  Register #(.width(2)) register_1 (.D(multiplexer_6_out), .en(1'b1), .clk(clk_i), .Q(register_1_q), .clr(reset_i));
  nand nand_1 (mot_tapis1_o, register_1_q[0], ~register_1_q[1]);  // NAND_Gate
  or or_1 (new_box_o, register_1_q[0], register_1_q[1]);

  // Notes on the sheet:
  //   Attention, votre version de Logisim
  //   ne contient pas de tracker. Si vous
  //   enregistrez votre projet, toutes les
  //   informations du tracker seront
  //   définitivement effacées.
endmodule

module code_lg_simulation (
  input  [7:0] val_compteur_i,
  output [1:0] code_o
);

  wire comparator_1_lt, comparator_2_lt, comparator_3_lt;
  wire [1:0] multiplexer_1_out, multiplexer_2_out;

  Multiplexer #(.width(2), .enable("false")) multiplexer_1 (
    .in0(2'b11), .in1(2'b10), .out(multiplexer_1_out), .sel(comparator_1_lt));
  Comparator comparator_1 (.a(val_compteur_i), .b(8'h20), .lt(comparator_1_lt));  // open: gt, eq
  Multiplexer #(.width(2), .enable("false")) multiplexer_2 (
    .in0(multiplexer_1_out), .in1(2'b01), .out(multiplexer_2_out), .sel(comparator_2_lt));
  Comparator comparator_2 (.a(val_compteur_i), .b(8'h14), .lt(comparator_2_lt));  // open: gt, eq
  Multiplexer #(.width(2), .enable("false")) multiplexer_3 (
    .in0(multiplexer_2_out), .in1(2'b00), .out(code_o), .sel(comparator_3_lt));
  Comparator comparator_3 (.a(val_compteur_i), .b(8'he), .lt(comparator_3_lt));  // open: gt, eq

  // Notes on the sheet:
  //   Attention, votre version de Logisim
  //   ne contient pas de tracker. Si vous
  //   enregistrez votre projet, toutes les
  //   informations du tracker seront
  //   définitivement effacées.
endmodule

module code_lg_integration (
  input  [7:0] val_compteur_i,
  output [1:0] code_o
);

  wire comparator_1_lt, comparator_2_lt, comparator_3_lt;
  wire [1:0] multiplexer_1_out, multiplexer_2_out;

  Multiplexer #(.width(2), .enable("false")) multiplexer_1 (
    .in0(2'b11), .in1(2'b10), .out(multiplexer_1_out), .sel(comparator_1_lt));
  Comparator comparator_1 (.a(val_compteur_i), .b(8'h18), .lt(comparator_1_lt));  // open: gt, eq
  Multiplexer #(.width(2), .enable("false")) multiplexer_2 (
    .in0(multiplexer_1_out), .in1(2'b01), .out(multiplexer_2_out), .sel(comparator_2_lt));
  Comparator comparator_2 (.a(val_compteur_i), .b(8'h11), .lt(comparator_2_lt));  // open: gt, eq
  Multiplexer #(.width(2), .enable("false")) multiplexer_3 (
    .in0(multiplexer_2_out), .in1(2'b00), .out(code_o), .sel(comparator_3_lt));
  Comparator comparator_3 (.a(val_compteur_i), .b(8'hc), .lt(comparator_3_lt));  // open: gt, eq

  // Notes on the sheet:
  //   Attention, votre version de Logisim
  //   ne contient pas de tracker. Si vous
  //   enregistrez votre projet, toutes les
  //   informations du tracker seront
  //   définitivement effacées.
endmodule
